# Fritzing sketch GC-Turbo (saved by Fritzing 0.9.3b)
perfboards: 1

parts:
  Part1 = Arduino Uno (Rev3)
  S2 = Tactile Switch Buttons - 12mm Square [package=tactile-pth-12mm]
  S3 = Tactile Switch Buttons - 12mm Square [package=tactile-pth-12mm]
  S4 = Tactile Switch Buttons - 12mm Square [package=tactile-pth-12mm]
  Part2 = Logic Level Converter
  Grove1 = Grove 4 Digit Display

nets:
  5V: Part1.5V, Part2.HV, Grove1.VCC
  GND: Part1.GND, S2.1, S2.3, S3.2, S3.4, S4.1, S4.3, Part2.GND, Grove1.GND
  N1: S2.2, S2.4
  N2: S3.1, S3.3
  N3: S4.2, S4.4
  N4: Grove1.DIO, Grove1.CLK

custom parts:
  Tactile Switch Buttons - 12mm Square: Medium-sized clicky momentary switches are standard input "buttons" on electronic projects. These work best in a PCB but can be used on a solderless breadboard as shown in this tutorial. The pins are normally open (disconnected) and when the button is pressed they are momentarily closed. They come in a pack of 10, they're pretty handy so you'll want to keep them around. You can find an EAGLE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
